// Logisim project FSM.circ as structural Verilog: 1 circuit, main circuit main
module main (
);

  wire and_1_out, and_2_out, and_3_out, and_4_out, clock_1_out, d_ff_1_q, d_ff_1_qn, d_ff_2_q, d_ff_3_q,
       d_ff_3_qn, nor_1_out, or_1_out, xor_1_out;

  Clock clock_1 (.out(clock_1_out));
  or or_1 (or_1_out, and_1_out, and_2_out);
  and and_1 (and_1_out, and_3_out, d_ff_1_qn);
  and and_2 (and_2_out, nor_1_out, d_ff_1_q);
  D_Flip_Flop d_ff_1 (.D(or_1_out), .clk(clock_1_out), .Q(d_ff_1_q), .Qn(d_ff_1_qn));  // open: preset, reset
  and and_3 (and_3_out, d_ff_3_q, d_ff_2_q);
  nor nor_1 (nor_1_out, d_ff_3_q, d_ff_2_q);
  xor xor_1 (xor_1_out, d_ff_3_q, d_ff_2_q);
  and and_4 (and_4_out, d_ff_1_qn, xor_1_out);
  D_Flip_Flop d_ff_2 (.D(and_4_out), .clk(clock_1_out), .Q(d_ff_2_q));  // open: Qn, preset, reset
  D_Flip_Flop d_ff_3 (.D(d_ff_3_qn), .clk(clock_1_out), .Q(d_ff_3_q), .Qn(d_ff_3_qn));  // open: preset, reset
endmodule
