// Logisim project ex1.circ as structural Verilog: 1 circuit, main circuit Split
module Split (
  input  [7:0] IN1,
  output OUT1,
  output OUT2,
  output [8:0] OUT3,
  output [8:0] OUT4
);

  wire xor_1_out, xor_2_out, xor_3_out, xor_4_out, xor_5_out, xor_6_out;
  wire [3:0] bitadder_1_out;
  wire [7:0] multiplexer_1_out, not_2_out;

  not not_1 (OUT3[8], OUT1);
  xor xor_1 (xor_1_out, IN1[0], IN1[1]);
  xor xor_2 (xor_2_out, IN1[2], IN1[3]);
  xor xor_3 (xor_3_out, IN1[4], IN1[5]);
  xor xor_4 (xor_4_out, IN1[6], IN1[7]);
  xor xor_5 (xor_5_out, xor_1_out, xor_2_out);
  xor xor_6 (xor_6_out, xor_3_out, xor_4_out);
  xor xor_7 (OUT1, xor_5_out, xor_6_out);
  BitAdder bitadder_1 (.in0(IN1), .out(bitadder_1_out));
  Multiplexer #(.width(8)) multiplexer_1 (.in0(IN1), .in1(not_2_out), .out(multiplexer_1_out), .sel(OUT2));
  assign not_2_out = ~IN1;  // NOT_Gate not_2, 8 bits wide
  Comparator #(.mode("unsigned"), .width(4)) comparator_1 (.a(bitadder_1_out), .b(4'b0100), .gt(OUT2));  // open: eq, lt
  Adder #(.width(9)) adder_1 (.a({OUT2, multiplexer_1_out}), .b({{8{1'b0}}, OUT2}), .out(OUT4));  // open: cin, cout

  assign OUT3[7:0] = IN1;

  // Other names for the same wires on the sheet: IN1_0 = IN1[0]; IN1_1 = IN1[1]; IN1_2 = IN1[2]; IN1_3 = IN1[3];
  //   IN1_4 = IN1[4]; IN1_5 = IN1[5]; IN1_6 = IN1[6]; IN1_7 = IN1[7]

  // Notes on the sheet:
  //   PUT CIRCUITRY HERE
endmodule
