// Logisim project ex2.circ as structural Verilog: 6 circuits, main circuit NOR1
module NAND1 (
  input  A,
  input  B,
  output RESULT
);

  wire and_1_out;

  and and_1 (and_1_out, A, B);
  not not_1 (RESULT, and_1_out);

  // Notes on the sheet:
  //   PUT CIRCUITRY HERE
endmodule

module NOR1 (
  input  A,
  input  B,
  output RESULT
);

  wire or_1_out;

  or or_1 (or_1_out, A, B);
  not not_1 (RESULT, or_1_out);

  // Notes on the sheet:
  //   PUT CIRCUITRY HERE
endmodule

module XOR1 (
  input  A,
  input  B,
  output RESULT
);

  wire not_1_out, not_2_out, or_1_out, or_2_out;

  not not_1 (not_1_out, B);
  not not_2 (not_2_out, A);
  or or_1 (or_1_out, A, not_1_out);
  or or_2 (or_2_out, not_2_out, B);
  NAND1 nand1_1 (.A(or_1_out), .B(or_2_out), .RESULT(RESULT));

  // Notes on the sheet:
  //   PUT CIRCUITRY HERE
endmodule

module MUX2 (
  input  A,
  input  B,
  input  Sel,
  output RESULT
);

  wire and_1_out, and_2_out, not_1_out;

  not not_1 (not_1_out, Sel);
  and and_1 (and_1_out, A, not_1_out);
  and and_2 (and_2_out, B, Sel);
  or or_1 (RESULT, and_1_out, and_2_out);

  // Notes on the sheet:
  //   PUT CIRCUITRY HERE
endmodule

module MUX4 (
  input  A,
  input  B,
  input  C,
  input  D,
  input  Sel1,
  input  Sel2,
  output RESULT
);

  wire mux2_1_result, mux2_2_result;

  MUX2 mux2_1 (.A(A), .B(B), .Sel(Sel1), .RESULT(mux2_1_result));
  MUX2 mux2_2 (.A(C), .B(D), .Sel(Sel1), .RESULT(mux2_2_result));
  MUX2 mux2_3 (.A(mux2_1_result), .B(mux2_2_result), .Sel(Sel2), .RESULT(RESULT));

  // Notes on the sheet:
  //   PUT CIRCUITRY HERE
endmodule

module Half_Adder (
  input  A,
  input  B,
  output SUM,
  output CARRY
);

  and and_1 (CARRY, A, B);
  XOR1 xor1_1 (.A(A), .B(B), .RESULT(SUM));
endmodule
