// Logisim project ex3.circ as structural Verilog: 3 circuits, main circuit rot1
module rot1 (
  input  [7:0] in_1,
  output [7:0] out_2
);


  assign out_2 = {in_1[0], in_1[7:1]};

  // Notes on the sheet:
  //   PUT CIRCUITRY HERE
endmodule

module Running_LED (
  input  [7:0] INITIAL_LED,
  input  RST,
  output [7:0] OUT_LED
);

  wire clock_1_out;
  wire [7:0] multiplexer_1_out, register_1_q;

  LED led_1 (.in(OUT_LED[7]));
  Register register_1 (.D(multiplexer_1_out), .clk(clock_1_out), .Q(register_1_q));  // open: en, clr
  Multiplexer #(.width(8)) multiplexer_1 (.in0(OUT_LED), .in1(INITIAL_LED), .out(multiplexer_1_out), .sel(RST));
  Clock clock_1 (.out(clock_1_out));
  LED led_2 (.in(OUT_LED[6]));
  LED led_3 (.in(OUT_LED[5]));
  rot1 rot1_1 (.in_1(register_1_q), .out_2(OUT_LED));
  LED led_4 (.in(OUT_LED[4]));
  LED led_5 (.in(OUT_LED[3]));
  LED led_6 (.in(OUT_LED[2]));
  LED led_7 (.in(OUT_LED[1]));
  LED led_8 (.in(OUT_LED[0]));

  // Notes on the sheet:
  //   PUT CIRCUITS HERE
endmodule

module task4 (
  input  [7:0] INITIAL_LED,
  input  RST,
  output [7:0] OUT_LED
);

  wire clock_1_out, not_1_out, t_ff_1_q, t_ff_2_q, t_ff_3_q, t_ff_4_q, t_ff_5_q, t_ff_6_q, t_ff_7_q, t_ff_8_q;
  wire [7:0] multiplexer_1_out, register_1_q;

  T_Flip_Flop t_ff_1 (.T(1'b1), .clk(clock_1_out), .Q(t_ff_1_q), .reset(RST));  // open: Qn, preset
  Clock clock_1 (.out(clock_1_out));
  T_Flip_Flop t_ff_2 (.T(t_ff_1_q), .clk(clock_1_out), .Q(t_ff_2_q), .reset(RST));  // open: Qn, preset
  LED led_1 (.in(OUT_LED[7]));
  Multiplexer #(.width(8)) multiplexer_1 (.in0(OUT_LED), .in1(INITIAL_LED), .out(multiplexer_1_out), .sel(RST));
  T_Flip_Flop t_ff_3 (.T(t_ff_2_q), .clk(clock_1_out), .Q(t_ff_3_q), .reset(RST));  // open: Qn, preset
  LED led_2 (.in(OUT_LED[6]));
  Register register_1 (.D(multiplexer_1_out), .en(not_1_out), .clk(clock_1_out), .Q(register_1_q));  // open: clr
  T_Flip_Flop t_ff_4 (.T(t_ff_3_q), .clk(clock_1_out), .Q(t_ff_4_q), .reset(RST));  // open: Qn, preset
  LED led_3 (.in(OUT_LED[5]));
  rot1 rot1_1 (.in_1(register_1_q), .out_2(OUT_LED));
  T_Flip_Flop t_ff_5 (.T(t_ff_4_q), .clk(clock_1_out), .Q(t_ff_5_q), .reset(RST));  // open: Qn, preset
  T_Flip_Flop t_ff_6 (.T(t_ff_5_q), .clk(clock_1_out), .Q(t_ff_6_q), .reset(RST));  // open: Qn, preset
  T_Flip_Flop t_ff_7 (.T(t_ff_6_q), .clk(clock_1_out), .Q(t_ff_7_q), .reset(RST));  // open: Qn, preset
  LED led_4 (.in(OUT_LED[4]));
  T_Flip_Flop t_ff_8 (.T(t_ff_7_q), .clk(clock_1_out), .Q(t_ff_8_q), .reset(RST));  // open: Qn, preset
  LED led_5 (.in(OUT_LED[3]));
  not not_1 (not_1_out, t_ff_8_q);
  LED led_6 (.in(OUT_LED[2]));
  LED led_7 (.in(OUT_LED[1]));
  LED led_8 (.in(OUT_LED[0]));

  // Notes on the sheet:
  //   PUT CIRCUITS HERE
endmodule
