// Logisim project proj_2_2.circ as structural Verilog: 6 circuits, main circuit testbench
module inst_fetch (
  input  clk,
  input  rst,
  input  control_en_i,
  input  [31:0] control_pc_i,
  input  [15:0] inst_i,
  output inst_en_o,
  output [31:0] current_pc_o,
  output [31:0] inst_addr_o,
  output [15:0] inst_o
);

  wire not_1_out, not_2_out;
  wire [31:0] adder_1_out, counter_1_q, multiplexer_1_out;

  not not_1 (not_1_out, rst);
  Adder #(.width(32)) adder_1 (.a(control_pc_i), .b(32'h1), .out(adder_1_out));  // open: cin, cout
  Counter #(.max('hffffffff), .width(32)) counter_1 (
    .clr(rst), .load(control_en_i), .up(not_1_out), .count(not_1_out), .clk(clk), .D(adder_1_out),
    .Q(counter_1_q));  // open: carry
  Multiplexer #(.width(32)) multiplexer_1 (
    .in0(counter_1_q), .in1(control_pc_i), .out(multiplexer_1_out), .sel(control_en_i));
  not not_2 (not_2_out, rst);
  Register #(.width(32)) register_1 (.D(multiplexer_1_out), .en(not_2_out), .clk(clk), .Q(current_pc_o), .clr(rst));
  not not_3 (inst_en_o, rst);

  assign inst_addr_o = current_pc_o;
  assign inst_o = inst_i;

  // Notes on the sheet:
  //   Don't touch
endmodule

module TOP (
  input  rst,
  input  clk,
  input  [15:0] inst,
  input  [31:0] mem_result,
  input  [31:0] current_pc,
  output mem_wen,
  output [31:0] mem_din,
  output mem_ren,
  output [31:0] alu_result,
  output control_en,
  output [31:0] control_pc,
  output wb_en,
  output [4:0] wb_addr,
  output [31:0] wb_data
);

  wire imm4;
  wire [1:0] opcode;
  wire [2:0] func3;
  wire [11:2] multiplexer_3_out;
  wire [31:0] multiplexer_1_out, multiplexer_2_out, regfile_1_read_data1, regfile_1_read_data2;

  RegFile regfile_1 (
    .read_data1(regfile_1_read_data1), .read_data2(regfile_1_read_data2));  // open: write_data, write_reg, we, read_reg1, read_reg2, clk, rst
  Multiplexer #(.width(32)) multiplexer_1 (
    .in0(regfile_1_read_data1), .in1(current_pc), .out(multiplexer_1_out));  // open: sel
  Multiplexer #(.width(32)) multiplexer_2 (.in0(regfile_1_read_data2), .out(multiplexer_2_out));  // open: in1, sel
  Multiplexer #(.width(16)) multiplexer_3 (
    .in0(inst), .in1({16{1'b0}}), .out({func3, imm4, multiplexer_3_out, opcode}), .sel(rst));
  ALU alu_1 (
    .opcode(opcode), .func3(func3), .imm4(imm4), .rs1(multiplexer_1_out), .rs2(multiplexer_2_out));  // open: imm, alu_result
  ImmGem immgem_1 (.inst({func3, imm4, multiplexer_3_out, opcode}));  // open: rd, rs1, rs2, imm

  // Notes on the sheet:
  //   Fixed I/O
  //   Don't touch
endmodule

module testbench (
  input  rst,
  output mem_wen,
  output [31:0] mem_din,
  output mem_ren,
  output [31:0] mem_addr,
  output control_en,
  output [31:0] control_pc,
  output halt,
  output wb_en,
  output [4:0] wb_addr,
  output [31:0] wb_data
);

  wire clk, inst_en, not_1_out, not_2_out, not_3_out, not_4_out, por_1_out, rst_t;
  wire [15:0] inst, inst_i;
  wire [31:0] current_pc, inst_addr, mem_result;

  not not_1 (not_1_out, inst_i[0]);
  not not_2 (not_2_out, inst_i[1]);
  not not_3 (not_3_out, inst_i[13]);
  not not_4 (not_4_out, inst_i[14]);
  and and_1 (halt, not_1_out, not_2_out, not_3_out, not_4_out, inst_i[15]);
  Clock clock_1 (.out(clk));
  or or_1 (rst_t, rst, por_1_out);
  POR por_1 (.out(por_1_out));
  inst_fetch inst_fetch_1 (
    .clk(clk), .rst(rst_t), .control_en_i(control_en), .control_pc_i(control_pc), .inst_i(inst_i),
    .inst_en_o(inst_en), .current_pc_o(current_pc), .inst_addr_o(inst_addr), .inst_o(inst));
  TOP top_1 (
    .rst(rst_t), .clk(clk), .inst(inst), .mem_result(mem_result), .current_pc(current_pc), .mem_wen(mem_wen),
    .mem_din(mem_din), .mem_ren(mem_ren), .alu_result(mem_addr), .control_en(control_en),
    .control_pc(control_pc), .wb_en(wb_en), .wb_addr(wb_addr), .wb_data(wb_data));
  ROM #(.dataWidth(16)) rom_1 (.addr(inst_addr[7:0]), .data(inst_i));
  RAM #(.addrWidth(16), .asyncread("true"), .clearpin("true"), .dataWidth(32), .\type ("nonvolatile")) ram_1 (
    .addr(mem_addr[15:0]), .we(mem_wen), .oe(mem_ren), .clk(clk), .din(mem_din), .dout(mem_result),
    .clr(rst_t));

  // Notes on the sheet:
  //   contents of rom_1 (hex, n*v repeats v):
  //   4409 147d c011 bffd 1 1 4111 5429 c422 44b5 48 8482 8526 414c 511 c148 8000
  //   you can write any instruction in
endmodule

module ImmGem (
  input  [15:0] inst,
  output [4:0] rd,
  output [4:0] rs1,
  output [4:0] rs2,
  output [31:0] imm
);


  // Other names for the same wires on the sheet: opcode[1:0] = inst[1:0]; func3[2:0] = inst[15:13]
endmodule

module ALU (
  input  [1:0] opcode,
  input  [2:0] func3,
  input  imm4,
  input  [31:0] rs1,
  input  [31:0] rs2,
  input  [31:0] imm,
  output [31:0] alu_result
);

  wire [26:0] multiplexer_1_out;
  wire [31:0] adder_1_out, adder_2_out, adder_3_out, adder_4_out, adder_5_out, adder_6_out,
       multiplexer_2_out, multiplexer_3_out, multiplexer_4_out, shifter_1_out, shifter_2_out;

  Multiplexer #(.width(27)) multiplexer_1 (.in0({27{1'b0}}), .in1({27{1'b1}}), .out(multiplexer_1_out), .sel(imm4));
  Adder #(.width(32)) adder_1 (.a(imm), .b(rs1), .out(adder_1_out));  // open: cin, cout
  Adder #(.width(32)) adder_2 (.a(rs2), .b({multiplexer_1_out, {5{1'b0}}}), .out(adder_2_out));  // open: cin, cout
  Adder #(.width(32)) adder_3 (.a(rs1), .b(adder_2_out), .out(adder_3_out));  // open: cin, cout
  Adder #(.width(32)) adder_4 (.a(imm), .b(rs1), .out(adder_4_out));  // open: cin, cout
  Shifter #(.width(32)) shifter_1 (.in(rs1), .\dist (rs2[4:0]), .out(shifter_1_out));
  Multiplexer #(.width(32)) multiplexer_2 (.in0(rs2), .in1(adder_5_out), .out(multiplexer_2_out), .sel(imm4));
  Adder #(.width(32)) adder_5 (.a(rs1), .b(rs2), .out(adder_5_out));  // open: cin, cout
  Adder #(.width(32)) adder_6 (.a(imm), .b(rs1), .out(adder_6_out));  // open: cin, cout
  Shifter #(.width(32)) shifter_2 (.in(adder_2_out), .\dist (5'b01100), .out(shifter_2_out));
  Multiplexer #(.select(3), .width(32)) multiplexer_3 (
    .in0(adder_3_out), .in2(adder_2_out), .in3(shifter_2_out), .in5(adder_4_out), .in6(adder_4_out),
    .out(multiplexer_3_out), .sel(func3));  // open: in1, in4, in7
  Multiplexer #(.select(3), .width(32)) multiplexer_4 (
    .in0(shifter_1_out), .in4(multiplexer_2_out), .in6(adder_6_out), .out(multiplexer_4_out), .sel(func3));  // open: in1, in2, in3, in5, in7
  Multiplexer #(.select(2), .width(32)) multiplexer_5 (
    .in0(adder_1_out), .in1(multiplexer_3_out), .in2(multiplexer_4_out), .out(alu_result), .sel(opcode));  // open: in3
endmodule

module RegFile (
  input  [31:0] write_data,
  input  [4:0] write_reg,
  input  we,
  input  [4:0] read_reg1,
  input  [4:0] read_reg2,
  input  clk,
  input  rst,
  output [31:0] read_data1,
  output [31:0] read_data2
);

  wire demultiplexer_1_out2, demultiplexer_1_out8, demultiplexer_1_out9, demultiplexer_1_out10,
       demultiplexer_1_out11, demultiplexer_1_out12, demultiplexer_1_out13, demultiplexer_1_out14,
       demultiplexer_1_out15;
  wire [31:0] x2, x8, x9, x10, x11, x12, x13, x14, x15;

  Demultiplexer #(.select(4)) demultiplexer_1 (
    .out2(demultiplexer_1_out2), .out8(demultiplexer_1_out8), .out9(demultiplexer_1_out9),
    .out10(demultiplexer_1_out10), .out11(demultiplexer_1_out11), .out12(demultiplexer_1_out12),
    .out13(demultiplexer_1_out13), .out14(demultiplexer_1_out14), .out15(demultiplexer_1_out15), .in(we),
    .sel(write_reg[3:0]));  // open: out0, out1, out3, out4, out5, out6, out7
  Register #(.width(32)) register_1 (.D(write_data), .en(demultiplexer_1_out2), .clk(clk), .Q(x2), .clr(rst));
  Register #(.width(32)) register_2 (.D(write_data), .en(demultiplexer_1_out8), .clk(clk), .Q(x8), .clr(rst));
  Register #(.width(32)) register_3 (.D(write_data), .en(demultiplexer_1_out9), .clk(clk), .Q(x9), .clr(rst));
  Register #(.width(32)) register_4 (.D(write_data), .en(demultiplexer_1_out10), .clk(clk), .Q(x10), .clr(rst));
  Register #(.width(32)) register_5 (.D(write_data), .en(demultiplexer_1_out11), .clk(clk), .Q(x11), .clr(rst));
  Register #(.width(32)) register_6 (.D(write_data), .en(demultiplexer_1_out12), .clk(clk), .Q(x12), .clr(rst));
  Register #(.width(32)) register_7 (.D(write_data), .en(demultiplexer_1_out13), .clk(clk), .Q(x13), .clr(rst));
  Register #(.width(32)) register_8 (.D(write_data), .en(demultiplexer_1_out14), .clk(clk), .Q(x14), .clr(rst));
  Register #(.width(32)) register_9 (.D(write_data), .en(demultiplexer_1_out15), .clk(clk), .Q(x15), .clr(rst));
  Multiplexer #(.select(4), .width(32)) multiplexer_1 (
    .in0({32{1'b0}}), .in2(x2), .in8(x8), .in9(x9), .in10(x10), .in11(x11), .in12(x12), .in13(x13),
    .in14(x14), .in15(x15), .out(read_data1), .sel(read_reg1[3:0]));  // open: in1, in3, in4, in5, in6, in7
  Multiplexer #(.select(4), .width(32)) multiplexer_2 (
    .in0({32{1'b0}}), .in2(x2), .in8(x8), .in9(x9), .in10(x10), .in11(x11), .in12(x12), .in13(x13),
    .in14(x14), .in15(x15), .out(read_data2), .sel(read_reg2[3:0]));  // open: in1, in3, in4, in5, in6, in7
endmodule
