// Logisim project proj_2_2.circ as structural Verilog: 6 circuits, main circuit testbench
module inst_fetch (
  input  clk,
  input  rst,
  input  control_en_i,
  input  [31:0] control_pc_i,
  input  [15:0] inst_i,
  output inst_en_o,
  output [31:0] current_pc_o,
  output [31:0] inst_addr_o,
  output [15:0] inst_o
);

  wire not_1_out, not_2_out;
  wire [31:0] adder_1_out, counter_1_q, multiplexer_1_out;

  not not_1 (not_1_out, rst);
  Adder #(.width(32)) adder_1 (.a(control_pc_i), .b(32'h1), .out(adder_1_out));  // open: cin, cout
  Counter #(.max('hffffffff), .width(32)) counter_1 (
    .clr(rst), .load(control_en_i), .up(not_1_out), .count(not_1_out), .clk(clk), .D(adder_1_out),
    .Q(counter_1_q));  // open: carry
  Multiplexer #(.width(32)) multiplexer_1 (
    .in0(counter_1_q), .in1(control_pc_i), .out(multiplexer_1_out), .sel(control_en_i));
  not not_2 (not_2_out, rst);
  Register #(.width(32)) register_1 (.D(multiplexer_1_out), .en(not_2_out), .clk(clk), .Q(current_pc_o), .clr(rst));
  not not_3 (inst_en_o, rst);

  assign inst_addr_o = current_pc_o;
  assign inst_o = inst_i;

  // Notes on the sheet:
  //   Don't touch
endmodule

module TOP (
  input  rst,
  input  clk,
  input  [15:0] inst,
  input  [31:0] mem_result,
  input  [31:0] current_pc,
  output mem_wen,
  output [31:0] mem_din,
  output mem_ren,
  output [31:0] alu_result,
  output control_en,
  output [31:0] control_pc,
  output wb_en,
  output [4:0] wb_addr,
  output [31:0] wb_data
);

  wire beq_z, beqz, comparator_2_eq, comparator_3_eq, mem_re, mem_we, multiplexer_6_out, multiplexer_7_out,
       not_1_out, op2_src, pc_ctrl, use_pc, we;
  wire [4:0] rd, rs1, rs2;
  wire [31:0] imm, multiplexer_1_out, multiplexer_2_out, multiplexer_3_out, multiplexer_4_out,
       multiplexer_5_out, multiplexer_8_out, multiplexer_9_out, regfile_1_read_data1, regfile_1_read_data2,
       res;

  Multiplexer #(.width(32)) multiplexer_1 (.in0(res), .in1(mem_result), .out(multiplexer_1_out), .sel(mem_re));
  RegFile regfile_1 (
    .write_data(multiplexer_1_out), .write_reg(rd), .we(we), .read_reg1(rs1), .read_reg2(rs2), .clk(clk),
    .rst(rst), .read_data1(regfile_1_read_data1), .read_data2(regfile_1_read_data2));
  Comparator #(.width(32)) comparator_1 (.a({32{1'b0}}), .b(regfile_1_read_data1), .eq(beq_z));  // open: gt, lt
  Multiplexer #(.width(32)) multiplexer_2 (
    .in0(regfile_1_read_data1), .in1(current_pc), .out(multiplexer_2_out), .sel(use_pc));
  Multiplexer #(.width(32)) multiplexer_3 (
    .in0(regfile_1_read_data2), .in1(imm), .out(multiplexer_3_out), .sel(op2_src));
  Adder #(.width(32)) adder_1 (.a(current_pc), .b(32'h1));  // open: out, cin, cout
  Multiplexer #(.width(32)) multiplexer_4 (.in0(current_pc), .in1(res), .out(multiplexer_4_out), .sel(pc_ctrl));
  Multiplexer #(.width(32)) multiplexer_5 (.in0({32{1'b0}}), .in1(res), .out(multiplexer_5_out), .sel(not_1_out));
  not not_1 (not_1_out, pc_ctrl);
  Multiplexer multiplexer_6 (.in0(1'b0), .in1(pc_ctrl), .out(multiplexer_6_out), .sel(multiplexer_7_out));
  Multiplexer multiplexer_7 (.in0(1'b1), .in1(beq_z), .out(multiplexer_7_out), .sel(beqz));
  ALU alu_1 (
    .opcode(inst[1:0]), .func3(inst[15:13]), .imm4(inst[12]), .rs1(multiplexer_2_out),
    .rs2(multiplexer_3_out), .alu_result(res));
  Multiplexer #(.width(32)) multiplexer_8 (
    .in0({32{1'b0}}), .in1(multiplexer_5_out), .out(multiplexer_8_out), .sel(we));
  Multiplexer #(.width(32)) multiplexer_9 (
    .in0({32{1'b0}}), .in1(regfile_1_read_data2), .out(multiplexer_9_out), .sel(mem_we));
  ImmGem immgem_1 (
    .inst(inst), .rd(rd), .rs1(rs1), .rs2(rs2), .imm(imm), .op2_src(op2_src), .pc_ctrl(pc_ctrl),
    .use_pc(use_pc), .we(we), .mem_we(mem_we), .mem_re(mem_re));
  Multiplexer multiplexer_10 (.in0(multiplexer_6_out), .in1(1'b0), .out(control_en), .sel(rst));
  Multiplexer #(.width(32)) multiplexer_11 (.in0(multiplexer_4_out), .in1({32{1'b0}}), .out(control_pc), .sel(rst));
  Multiplexer #(.width(32)) multiplexer_12 (.in0(multiplexer_8_out), .in1({32{1'b0}}), .out(wb_data), .sel(rst));
  Multiplexer #(.width(32)) multiplexer_13 (.in0(multiplexer_5_out), .in1({32{1'b0}}), .out(alu_result), .sel(rst));
  Multiplexer multiplexer_14 (.in0(we), .in1(1'b0), .out(wb_en), .sel(rst));
  Multiplexer #(.width(5)) multiplexer_15 (.in0(rd), .in1({5{1'b0}}), .out(wb_addr), .sel(rst));
  Multiplexer #(.width(32)) multiplexer_16 (.in0(multiplexer_9_out), .in1({32{1'b0}}), .out(mem_din), .sel(rst));
  Multiplexer multiplexer_17 (.in0(mem_we), .in1(1'b0), .out(mem_wen), .sel(rst));
  Multiplexer multiplexer_18 (.in0(mem_re), .in1(1'b0), .out(mem_ren), .sel(rst));
  Comparator #(.width(2)) comparator_2 (.a(inst[1:0]), .b(2'b01), .eq(comparator_2_eq));  // open: gt, lt
  Comparator #(.width(3)) comparator_3 (.a(inst[15:13]), .b(3'b110), .eq(comparator_3_eq));  // open: gt, lt
  and and_1 (beqz, comparator_2_eq, comparator_3_eq);

  // Other names for the same wires on the sheet: opcode[1:0] = inst[1:0]; imm4 = inst[12]; func3[2:0] = inst[15:13]

  // Notes on the sheet:
  //   Fixed I/O
  //   Don't touch
endmodule

module testbench (
  input  rst,
  output mem_wen,
  output [31:0] mem_din,
  output mem_ren,
  output [31:0] mem_addr,
  output control_en,
  output [31:0] control_pc,
  output halt,
  output wb_en,
  output [4:0] wb_addr,
  output [31:0] wb_data
);

  wire clk, inst_en, not_1_out, not_2_out, not_3_out, not_4_out, por_1_out, rst_t;
  wire [15:0] inst, inst_i;
  wire [31:0] current_pc, inst_addr, mem_result;

  not not_1 (not_1_out, inst_i[0]);
  not not_2 (not_2_out, inst_i[1]);
  not not_3 (not_3_out, inst_i[13]);
  not not_4 (not_4_out, inst_i[14]);
  and and_1 (halt, not_1_out, not_2_out, not_3_out, not_4_out, inst_i[15]);
  Clock clock_1 (.out(clk));
  or or_1 (rst_t, rst, por_1_out);
  POR por_1 (.out(por_1_out));
  inst_fetch inst_fetch_1 (
    .clk(clk), .rst(rst_t), .control_en_i(control_en), .control_pc_i(control_pc), .inst_i(inst_i),
    .inst_en_o(inst_en), .current_pc_o(current_pc), .inst_addr_o(inst_addr), .inst_o(inst));
  TOP top_1 (
    .rst(rst_t), .clk(clk), .inst(inst), .mem_result(mem_result), .current_pc(current_pc), .mem_wen(mem_wen),
    .mem_din(mem_din), .mem_ren(mem_ren), .alu_result(mem_addr), .control_en(control_en),
    .control_pc(control_pc), .wb_en(wb_en), .wb_addr(wb_addr), .wb_data(wb_data));
  ROM #(.dataWidth(16)) rom_1 ();  // open: addr, data
  ROM #(.dataWidth(16)) rom_2 (.addr(inst_addr[7:0]), .data(inst_i));
  RAM #(.addrWidth(16), .asyncread("true"), .clearpin("true"), .dataWidth(32), .\type ("nonvolatile")) ram_1 (
    .addr(mem_addr[15:0]), .we(mem_wen), .oe(mem_ren), .clk(clk), .din(mem_din), .dout(mem_result),
    .clr(rst_t));

  // Notes on the sheet:
  //   contents of rom_1 (hex, n*v repeats v):
  //   4429 4491 c0c0 40c8 1000 1 4111 5429 c422 44b5 48 8482 8526 414c 511 c148 8000
  //   contents of rom_2 (hex, n*v repeats v):
  //   4429 4491 c0c0 40c8 1000 1 4111 5429 c422 44b5 48 8482 8526 414c 511 c148 8000
  //   you can write any instruction in
  //   you can write any instruction in
endmodule

module ImmGem (
  input  [15:0] inst,
  output [4:0] rd,
  output [4:0] rs1,
  output [4:0] rs2,
  output [31:0] imm,
  output op2_src,
  output pc_ctrl,
  output use_pc,
  output we,
  output mem_we,
  output mem_re
);

  wire add, addi, addi4spn, and_1_out, and_6_out, beqz, CI, comparator_1_eq, comparator_2_eq,
       comparator_3_eq, comparator_4_eq, comparator_5_eq, comparator_6_eq, comparator_7_eq, comparator_8_eq,
       comparator_9_eq, comparator_10_eq, comparator_11_eq, comparator_12_eq, comparator_13_eq,
       comparator_14_eq, comparator_15_eq, comparator_16_eq, comparator_17_eq, comparator_18_eq,
       comparator_19_eq, comparator_20_eq, comparator_21_eq, comparator_22_eq, comparator_23_eq,
       comparator_24_eq, j, jr, li, lui, mv, not_1_out, not_2_out, or_1_out, or_2_out, slli, sw, swsp, use_2,
       use_rd, use_rd_8, use_rs1, use_rs1_8, use_rs2;
  wire [4:0] adder_1_out, adder_2_out, adder_3_out, bit_extender_1_out, bit_extender_3_out,
       bit_extender_10_out, multiplexer_2_out, multiplexer_3_out, multiplexer_4_out, multiplexer_11_out,
       multiplexer_14_out;
  wire [31:0] bit_extender_2_out, bit_extender_4_out, bit_extender_5_out, bit_extender_6_out,
       bit_extender_7_out, bit_extender_8_out, bit_extender_9_out, bit_extender_11_out, CI_imm,
       multiplexer_1_out, multiplexer_5_out, multiplexer_8_out, multiplexer_9_out, multiplexer_10_out,
       multiplexer_12_out, multiplexer_13_out, shifter_1_out;

  assign bit_extender_1_out = {{2{1'b0}}, inst[9:7]};  // Bit_Extender bit_extender_1
  assign bit_extender_2_out = {{23{inst[11]}}, {inst[11], inst[6:5], inst[2], inst[10:9], inst[4:3], 1'b0}};  // Bit_Extender bit_extender_2
  assign bit_extender_3_out = {{2{1'b0}}, inst[4:2]};  // Bit_Extender bit_extender_3
  Comparator #(.width(5)) comparator_1 (.a(inst[6:2]), .b({5{1'b0}}), .eq(comparator_1_eq));  // open: gt, lt
  not not_1 (not_1_out, comparator_1_eq);
  Comparator #(.width(2)) comparator_2 (.a(inst[1:0]), .b(2'b10), .eq(comparator_2_eq));  // open: gt, lt
  Comparator #(.width(3)) comparator_3 (.a(inst[15:13]), .b(3'b100), .eq(comparator_3_eq));  // open: gt, lt
  Comparator #(.width(1)) comparator_4 (.a(inst[12]), .b(1'b0), .eq(comparator_4_eq));  // open: gt, lt
  not not_2 (not_2_out, comparator_4_eq);
  Comparator #(.width(2)) comparator_5 (.a(inst[1:0]), .b(2'b01), .eq(comparator_5_eq));  // open: gt, lt
  Comparator #(.width(3)) comparator_6 (.a(inst[15:13]), .b(3'b000), .eq(comparator_6_eq));  // open: gt, lt
  Comparator #(.width(2)) comparator_7 (.a(inst[1:0]), .b(2'b10), .eq(comparator_7_eq));  // open: gt, lt
  Comparator #(.width(3)) comparator_8 (.a(inst[15:13]), .b(3'b000), .eq(comparator_8_eq));  // open: gt, lt
  Comparator #(.width(2)) comparator_9 (.a(inst[1:0]), .b(2'b01), .eq(comparator_9_eq));  // open: gt, lt
  Comparator #(.width(3)) comparator_10 (.a(inst[15:13]), .b(3'b010), .eq(comparator_10_eq));  // open: gt, lt
  Comparator #(.width(2)) comparator_11 (.a(inst[1:0]), .b(2'b01), .eq(comparator_11_eq));  // open: gt, lt
  Comparator #(.width(3)) comparator_12 (.a(inst[15:13]), .b(3'b011), .eq(comparator_12_eq));  // open: gt, lt
  Adder #(.width(5)) adder_1 (.a(bit_extender_1_out), .b(5'b01000), .out(adder_1_out));  // open: cin, cout
  Multiplexer #(.width(32)) multiplexer_1 (
    .in0({32{1'b0}}), .in1(bit_extender_2_out), .out(multiplexer_1_out), .sel(beqz));
  Multiplexer #(.width(5)) multiplexer_2 (.in0({5{1'b0}}), .in1(adder_2_out), .out(multiplexer_2_out), .sel(use_rd_8));
  Adder #(.width(5)) adder_2 (.a(bit_extender_3_out), .b(5'b01000), .out(adder_2_out));  // open: cin, cout
  and and_1 (and_1_out, comparator_2_eq, comparator_3_eq);
  and and_2 (addi, comparator_5_eq, comparator_6_eq);
  and and_3 (slli, comparator_7_eq, comparator_8_eq);
  and and_4 (li, comparator_9_eq, comparator_10_eq);
  and and_5 (lui, comparator_11_eq, comparator_12_eq);
  Multiplexer #(.width(5)) multiplexer_3 (.in0({5{1'b0}}), .in1(adder_1_out), .out(multiplexer_3_out), .sel(use_rs1_8));
  assign bit_extender_4_out = {{20{inst[12]}}, {inst[12], inst[8], inst[10:9], inst[6], inst[7], inst[2], inst[11], inst[5:3], 1'b0}};  // Bit_Extender bit_extender_4
  and and_6 (and_6_out, and_1_out, comparator_4_eq);
  and and_7 (add, and_1_out, not_2_out);
  Multiplexer #(.width(5)) multiplexer_4 (
    .in0(multiplexer_3_out), .in1(5'b00010), .out(multiplexer_4_out), .sel(use_2));
  Multiplexer #(.width(32)) multiplexer_5 (
    .in0(multiplexer_1_out), .in1(bit_extender_4_out), .out(multiplexer_5_out), .sel(j));
  Multiplexer #(.width(5)) multiplexer_6 (.in0(multiplexer_2_out), .in1(inst[11:7]), .out(rd), .sel(use_rd));
  and and_8 (jr, comparator_1_eq, and_6_out);
  and and_9 (mv, not_1_out, and_6_out);
  Multiplexer #(.width(5)) multiplexer_7 (.in0(multiplexer_4_out), .in1(inst[11:7]), .out(rs1), .sel(use_rs1));
  assign bit_extender_5_out = {{22{1'b0}}, {inst[10:7], inst[12:11], inst[5], inst[6], 2'b00}};  // Bit_Extender bit_extender_5
  Multiplexer #(.width(32)) multiplexer_8 (
    .in0(multiplexer_5_out), .in1(bit_extender_5_out), .out(multiplexer_8_out), .sel(addi4spn));
  Multiplexer #(.width(32)) multiplexer_9 (
    .in0({32{1'b0}}), .in1(bit_extender_6_out), .out(multiplexer_9_out), .sel(slli));
  assign bit_extender_6_out = {{26{1'b0}}, {inst[12], inst[6:2]}};  // Bit_Extender bit_extender_6
  assign bit_extender_7_out = {{24{1'b0}}, {inst[8:7], inst[12:9], 2'b00}};  // Bit_Extender bit_extender_7
  Comparator #(.width(2)) comparator_13 (.a(inst[1:0]), .b(2'b10), .eq(comparator_13_eq));  // open: gt, lt
  Comparator #(.width(3)) comparator_14 (.a(inst[15:13]), .b(3'b110), .eq(comparator_14_eq));  // open: gt, lt
  Comparator #(.width(2)) comparator_15 (.a(inst[1:0]), .b(2'b00), .eq(comparator_15_eq));  // open: gt, lt
  Comparator #(.width(3)) comparator_16 (.a(inst[15:13]), .b(3'b000), .eq(comparator_16_eq));  // open: gt, lt
  Comparator #(.width(2)) comparator_17 (.a(inst[1:0]), .b(2'b00), .eq(comparator_17_eq));  // open: gt, lt
  Comparator #(.width(3)) comparator_18 (.a(inst[15:13]), .b(3'b010), .eq(comparator_18_eq));  // open: gt, lt
  Comparator #(.width(2)) comparator_19 (.a(inst[1:0]), .b(2'b00), .eq(comparator_19_eq));  // open: gt, lt
  Comparator #(.width(3)) comparator_20 (.a(inst[15:13]), .b(3'b110), .eq(comparator_20_eq));  // open: gt, lt
  Comparator #(.width(2)) comparator_21 (.a(inst[1:0]), .b(2'b01), .eq(comparator_21_eq));  // open: gt, lt
  Comparator #(.width(3)) comparator_22 (.a(inst[15:13]), .b(3'b110), .eq(comparator_22_eq));  // open: gt, lt
  Comparator #(.width(2)) comparator_23 (.a(inst[1:0]), .b(2'b01), .eq(comparator_23_eq));  // open: gt, lt
  Comparator #(.width(3)) comparator_24 (.a(inst[15:13]), .b(3'b101), .eq(comparator_24_eq));  // open: gt, lt
  Multiplexer #(.width(32)) multiplexer_10 (
    .in0(multiplexer_8_out), .in1(bit_extender_7_out), .out(multiplexer_10_out), .sel(swsp));
  Multiplexer #(.width(5)) multiplexer_11 (.in0({5{1'b0}}), .in1(inst[11:7]), .out(multiplexer_11_out), .sel(jr));
  and and_10 (swsp, comparator_13_eq, comparator_14_eq);
  and and_11 (addi4spn, comparator_15_eq, comparator_16_eq);
  and and_12 (mem_re, comparator_17_eq, comparator_18_eq);
  and and_13 (sw, comparator_19_eq, comparator_20_eq);
  and and_14 (beqz, comparator_21_eq, comparator_22_eq);
  and and_15 (j, comparator_23_eq, comparator_24_eq);
  assign bit_extender_8_out = {{26{inst[12]}}, {inst[12], inst[6:2]}};  // Bit_Extender bit_extender_8
  assign bit_extender_9_out = {{25{1'b0}}, {inst[5], inst[12:10], inst[6], 2'b00}};  // Bit_Extender bit_extender_9
  assign bit_extender_10_out = {{2{1'b0}}, inst[4:2]};  // Bit_Extender bit_extender_10
  Multiplexer #(.width(32)) multiplexer_12 (
    .in0(multiplexer_9_out), .in1(shifter_1_out), .out(multiplexer_12_out), .sel(lui));
  Shifter #(.width(32)) shifter_1 (.in(bit_extender_8_out), .\dist (5'b01100), .out(shifter_1_out));
  Multiplexer #(.width(32)) multiplexer_13 (
    .in0(multiplexer_10_out), .in1(bit_extender_9_out), .out(multiplexer_13_out), .sel(or_1_out));
  or or_1 (or_1_out, mem_re, sw);
  Multiplexer #(.width(5)) multiplexer_14 (
    .in0(multiplexer_11_out), .in1(adder_3_out), .out(multiplexer_14_out), .sel(sw));
  Adder #(.width(5)) adder_3 (.a(bit_extender_10_out), .b(5'b01000), .out(adder_3_out));  // open: cin, cout
  Multiplexer #(.width(32)) multiplexer_15 (.in0(multiplexer_13_out), .in1(CI_imm), .out(imm), .sel(CI));
  Multiplexer #(.width(32)) multiplexer_16 (
    .in0(multiplexer_12_out), .in1(bit_extender_11_out), .out(CI_imm), .sel(or_2_out));
  assign bit_extender_11_out = {{26{inst[12]}}, {inst[12], inst[6:2]}};  // Bit_Extender bit_extender_11
  or or_2 (or_2_out, addi, li);
  Multiplexer #(.width(5)) multiplexer_17 (.in0(multiplexer_14_out), .in1(inst[6:2]), .out(rs2), .sel(use_rs2));
  or or_3 (use_rs1, mv, add, addi, slli, li, lui);
  or or_4 (use_2, swsp, addi4spn);
  or or_5 (use_rs1_8, mem_re, beqz, sw);
  or or_6 (use_rd, add, mv, addi, slli, li, lui);
  or or_7 (use_rd_8, addi4spn, mem_re, sw);
  or or_8 (use_rs2, add, swsp, mv);
  or or_9 (CI, addi, slli, li, lui);
  or or_10 (use_pc, beqz, j);
  or or_11 (pc_ctrl, beqz, j, jr);
  or or_12 (op2_src, addi, slli, li, lui, beqz, j, swsp, addi4spn, mem_re, sw);
  or or_13 (we, add, mv, addi, slli, li, lui, mem_re, addi4spn);
  or or_14 (mem_we, swsp, sw);

  // Other names for the same wires on the sheet: opcode[1:0] = inst[1:0]; func3[2:0] = inst[15:13]; lw = mem_re;
  //   use_rs2_8 = sw
endmodule

module ALU (
  input  [1:0] opcode,
  input  [2:0] func3,
  input  imm4,
  input  [31:0] rs1,
  input  [31:0] rs2,
  output [31:0] alu_result
);

  wire [31:0] adder_1_out, adder_2_out, adder_3_out, adder_4_out, adder_5_out, multiplexer_1_out,
       multiplexer_2_out, multiplexer_3_out, shifter_1_out;

  Adder #(.width(32)) adder_1 (.a(rs1), .b(rs2), .out(adder_1_out));  // open: cin, cout
  Adder #(.width(32)) adder_2 (.a(rs1), .b(rs2), .out(adder_2_out));  // open: cin, cout
  Adder #(.width(32)) adder_3 (.a(rs1), .b(rs2), .out(adder_3_out));  // open: cin, cout
  Adder #(.width(32)) adder_4 (.a(rs1), .b(rs2), .out(adder_4_out));  // open: cin, cout
  Shifter #(.width(32)) shifter_1 (.in(rs1), .\dist (rs2[4:0]), .out(shifter_1_out));
  Adder #(.width(32)) adder_5 (.a(rs1), .b(rs2), .out(adder_5_out));  // open: cin, cout
  Multiplexer #(.width(32)) multiplexer_1 (.in0(rs2), .in1(adder_5_out), .out(multiplexer_1_out), .sel(imm4));
  Multiplexer #(.select(3), .width(32)) multiplexer_2 (
    .in0(adder_3_out), .in1({32{1'b0}}), .in2(rs2), .in3(rs2), .in4({32{1'b0}}), .in5(adder_4_out),
    .in6(adder_4_out), .in7({32{1'b0}}), .out(multiplexer_2_out), .sel(func3));
  Multiplexer #(.select(3), .width(32)) multiplexer_3 (
    .in0(shifter_1_out), .in1({32{1'b0}}), .in2({32{1'b0}}), .in3({32{1'b0}}), .in4(multiplexer_1_out),
    .in5({32{1'b0}}), .in6(adder_1_out), .in7({32{1'b0}}), .out(multiplexer_3_out), .sel(func3));
  Multiplexer #(.select(2), .width(32)) multiplexer_4 (
    .in0(adder_2_out), .in1(multiplexer_2_out), .in2(multiplexer_3_out), .out(alu_result), .sel(opcode));  // open: in3
endmodule

module RegFile (
  input  [31:0] write_data,
  input  [4:0] write_reg,
  input  we,
  input  [4:0] read_reg1,
  input  [4:0] read_reg2,
  input  clk,
  input  rst,
  output [31:0] read_data1,
  output [31:0] read_data2
);

  wire demultiplexer_1_out2, demultiplexer_1_out8, demultiplexer_1_out9, demultiplexer_1_out10,
       demultiplexer_1_out11, demultiplexer_1_out12, demultiplexer_1_out13, demultiplexer_1_out14,
       demultiplexer_1_out15;
  wire [31:0] x2, x8, x9, x10, x11, x12, x13, x14, x15;

  Demultiplexer #(.select(4)) demultiplexer_1 (
    .out2(demultiplexer_1_out2), .out8(demultiplexer_1_out8), .out9(demultiplexer_1_out9),
    .out10(demultiplexer_1_out10), .out11(demultiplexer_1_out11), .out12(demultiplexer_1_out12),
    .out13(demultiplexer_1_out13), .out14(demultiplexer_1_out14), .out15(demultiplexer_1_out15), .in(we),
    .sel(write_reg[3:0]));  // open: out0, out1, out3, out4, out5, out6, out7
  Register #(.width(32)) register_1 (.D(write_data), .en(demultiplexer_1_out2), .clk(clk), .Q(x2), .clr(rst));
  Register #(.width(32)) register_2 (.D(write_data), .en(demultiplexer_1_out8), .clk(clk), .Q(x8), .clr(rst));
  Register #(.width(32)) register_3 (.D(write_data), .en(demultiplexer_1_out9), .clk(clk), .Q(x9), .clr(rst));
  Register #(.width(32)) register_4 (.D(write_data), .en(demultiplexer_1_out10), .clk(clk), .Q(x10), .clr(rst));
  Register #(.width(32)) register_5 (.D(write_data), .en(demultiplexer_1_out11), .clk(clk), .Q(x11), .clr(rst));
  Register #(.width(32)) register_6 (.D(write_data), .en(demultiplexer_1_out12), .clk(clk), .Q(x12), .clr(rst));
  Register #(.width(32)) register_7 (.D(write_data), .en(demultiplexer_1_out13), .clk(clk), .Q(x13), .clr(rst));
  Register #(.width(32)) register_8 (.D(write_data), .en(demultiplexer_1_out14), .clk(clk), .Q(x14), .clr(rst));
  Register #(.width(32)) register_9 (.D(write_data), .en(demultiplexer_1_out15), .clk(clk), .Q(x15), .clr(rst));
  Multiplexer #(.select(4), .width(32)) multiplexer_1 (
    .in0({32{1'b0}}), .in2(x2), .in8(x8), .in9(x9), .in10(x10), .in11(x11), .in12(x12), .in13(x13),
    .in14(x14), .in15(x15), .out(read_data1), .sel(read_reg1[3:0]));  // open: in1, in3, in4, in5, in6, in7
  Multiplexer #(.select(4), .width(32)) multiplexer_2 (
    .in0({32{1'b0}}), .in2(x2), .in8(x8), .in9(x9), .in10(x10), .in11(x11), .in12(x12), .in13(x13),
    .in14(x14), .in15(x15), .out(read_data2), .sel(read_reg2[3:0]));  // open: in1, in3, in4, in5, in6, in7
endmodule
